// Digital circuit CPU.dig as structural Verilog
module CPU (
  input  in_11,
  input  in_17,
  input  in_18,
  input  in_21,
  input  in_22,
  input  CLK_RAW,
  output [31:0] x8_s0_fp,
  output [31:0] x9_s1,
  output [31:0] x10_a0,
  output [31:0] PC,
  output [31:0] ADDR,
  output [31:0] Instr,
  output [7:0] Dout,
  output [4:0] Step,
  output [7:0] Substep,
  output [7:0] Dval,
  output [15:0] out_12,
  output [15:0] out_13,
  output [31:0] A,
  output [31:0] B,
  output [31:0] Result,
  output [31:0] out_19,
  output [11:0] CSR_Address,
  output [31:0] x11_a1,
  output [31:0] x4_tp,
  output [31:0] x5_t0,
  output [31:0] x6_t1,
  output [31:0] x7_t2,
  output [31:0] x1_ra,
  output [31:0] x2_sp,
  output [31:0] x3_gp,
  output [31:0] x12_a2,
  output [31:0] x13_a3,
  output [31:0] x14_a4,
  output [31:0] x15_a5,
  output [5:0] out_36
);

  wire ADDR_CLK, ADDR_IN, ADDR_LATCH, ALU_A, ALU_B, ALU_FLAG_LATCH, ALU_N, alu_shift_step_1_nsh_output,
       alu_shift_step_1_sh_loadlen, alu_shift_step_1_sh_reset, and_1_out, B_INSTR, B_RUN, B_STEP, B_STOP,
       B_SUBSTEP, BUS_CLK, BUS_EN, BUT_STOP, CLK, clock_1_lastsubstep, comparator_1_eq, comparator_1_gt,
       comparator_1_lt, Const1, Const31, CSR_OUT, d_ff_1_q, ImmB, ImmCSR, ImmI, ImmJ, ImmS, ImmU, IRQ_OP,
       IRQ_OP_SnP, LASTSTEP, MEM_IN, MEM_OUT, MEPC_OUT, MTVEC_OUT, multiplexer_1_out, nADDR_PE, nALU_RESET,
       nand_1_out, nCLK, nMEM_OE, nMEM_WE, nOPDONE, not_1_out, nPC_CNT_PE, nREG_IN_EN, nRESET, nS_EXT,
       nSTEPDONE, OP_IMM_LATCH, OP_IN, OP_IN_MUX, OP_LATCH, PC_IN, PC_IN_LATCH, PC_OUT, PC_OUT_SnP, REG_IN,
       RESET, ROM_SEL, RS1, Running;
  wire [1:0] ALU_A_MUX, LEN, opcode_1_trap2, REG_IN_MUX;
  wire [2:0] ALU_B_MUX, ALU_OP;
  wire [3:0] RSA, RSB, RSD;
  wire [7:0] ROM_DATA, ROM_DIN;
  wire [15:0] ROM_ADDR;
  wire [31:12] MicroCode_d;

  Register_view register_view_1 (
    .BUS_CLK(BUS_CLK), .nREG_IN_EN(nREG_IN_EN), .REG_IN(REG_IN), .RSD(RSD), .x1_ra(x1_ra), .x2_sp(x2_sp),
    .x3_gp(x3_gp), .x4_tp(x4_tp), .x5_t0(x5_t0), .x6_t1(x6_t1), .x7_t2(x7_t2), .x8_s0_fp(x8_s0_fp),
    .x9_s1(x9_s1), .x10_a0(x10_a0), .x11_a1(x11_a1), .x12_a2(x12_a2), .x13_a3(x13_a3), .x14_a4(x14_a4),
    .x15_a5(x15_a5));
  nand nand_1 (nand_1_out, PC_OUT_SnP, OP_IN_MUX);
  Multiplexer multiplexer_1 (.sel(out_12[12]), .in_0(RS1), .in_1(ImmCSR), .out(multiplexer_1_out));
  Comparator #(.Bits(32)) comparator_1 (
    .a(x3_gp), .b(32'h1), .gt(comparator_1_gt), .eq(comparator_1_eq), .lt(comparator_1_lt));
  LED led_1 (.in(Running));
  LED led_2 (.in(not_1_out));
  not not_1 (not_1_out, Running);
  Button #(.activeLow("true")) Stop (.out(BUT_STOP));
  Button #(.activeLow("true")) Run (.out(B_RUN));
  Button #(.activeLow("true")) One_Instruction (.out(B_INSTR));
  Button #(.activeLow("true")) One_Step (.out(B_STEP));
  Button #(.activeLow("true")) One_Substep (.out(B_SUBSTEP));
  LED led_3 (.in(comparator_1_gt));
  LED led_4 (.in(comparator_1_eq));
  CSR csr_1 (
    .CLK(BUS_CLK), .INA(multiplexer_1_out), .INB(in_22), .CSR_FUNC(out_12[11:10]), .ADDR_IN(ImmI),
    .ADDR_LATCH(in_21), .nRESET(nRESET), .NEW_VAL(CSR_OUT), .ADDR(CSR_Address));
  // Interrupt_Controller interrupt_controller_1: pin names not known; wires that end beside it: BUS_CLK, PC_OUT, nand_1_out, IRQ_OP_SnP, in_18, LASTSTEP, in_17, OP_LATCH, RESET, nRESET, MEPC_OUT, IRQ_OP, MTVEC_OUT, OP_IN_MUX, out_19
  and and_1 (and_1_out, nRESET, nOPDONE);
  D_FF #(.Default(1)) d_ff_1 (.D(comparator_1_lt), .C(~nOPDONE), .Q(d_ff_1_q));  // open: nQ
  D_FF_AS d_ff_as_1 (.Set(~1'b1), .D(1'b1), .C(ADDR_LATCH), .Clr(~and_1_out), .Q(IRQ_OP_SnP));  // open: nQ
  and and_2 (B_STOP, d_ff_1_q, BUT_STOP);
  DebugShift32 debugshift32_1 (.CLK(BUS_CLK), .D(ALU_A), .nEN(1'b0), .Val(A));
  DebugShift32 debugshift32_2 (.CLK(BUS_CLK), .D(ALU_B), .nEN(1'b0), .Val(B));
  DebugShift32 debugshift32_3 (.CLK(BUS_CLK), .D(ADDR_IN), .nEN(1'b0), .Val(Result));
  Reset reset_1 (.out(nRESET));
  Reset #(.invertOutput("false")) reset_2 (.out(RESET));
  Multiplexer multiplexer_2 (.sel(in_11), .in_0(ADDR_IN), .in_1(MEPC_OUT), .out(PC_IN));
  Multiplexer multiplexer_3 (.sel(OP_IN_MUX), .in_0(MEM_OUT), .in_1(IRQ_OP), .out(OP_IN));
  D_FF d_ff_2 (.D(OP_LATCH), .C(CLK), .Q(OP_IMM_LATCH));  // open: nQ
  Multiplexer #(.Selector_Bits(2)) multiplexer_4 (
    .sel(ALU_A_MUX), .in_0(RS1), .in_1(PC_OUT), .in_2(Const31), .in_3(1'b0), .out(ALU_A));
  not not_2 (nPC_CNT_PE, PC_IN_LATCH);
  Clock_driver clock_driver_1 (
    .CLK_RAW(CLK_RAW), .Stop(B_STOP), .Run(B_RUN), .One_Instruction(B_INSTR), .One_Step(B_STEP),
    .One_Substep(B_SUBSTEP), .nSTEPDONE(nSTEPDONE), .nOPDONE(nOPDONE), .nRESET(nRESET), .CLK(CLK),
    .nCLK(nCLK), .Running(Running));
  ALU_shift_step alu_shift_step_1 (
    .nCLK(nCLK), .nRESET(nALU_RESET), .nEN(nSTEPDONE), .SH_LOADLEN(alu_shift_step_1_sh_loadlen),
    .nSH_OUTPUT(alu_shift_step_1_nsh_output), .SH_RESET(alu_shift_step_1_sh_reset));
  PC pc_1 (
    .CLK(CLK), .BUS_CLK(BUS_CLK), .IN(PC_IN), .LATCH_IN(PC_IN_LATCH), .LATCH_OUT(LASTSTEP),
    .SnP_OUT(PC_OUT_SnP), .nPE_CNT(nPC_CNT_PE), .EN_CNT(OP_LATCH), .nRESET(nRESET), .OUT(PC_OUT), .PC(PC));
  OpCode opcode_1 (
    .CLK(BUS_CLK), .IN(OP_IN), .OP_LATCH(OP_LATCH), .IMM_LATCH(OP_IMM_LATCH), .IMM_SnP(BUS_EN),
    .nRESET(nRESET), .ImmI(ImmI), .ImmS(ImmS), .ImmB(ImmB), .ImmU(ImmU), .ImmJ(ImmJ), .Const1(Const1),
    .Const31(Const31), .ImmCSR(ImmCSR), .RSA(RSA), .RSB(RSB), .RSD(RSD), .OPCODE(out_12[9:5]),
    .FUNC3(out_12[12:10]), .ALU_SA(out_12[13]), .nS_EXT(nS_EXT), .SYS(out_12[15]), .TRAP2(opcode_1_trap2),
    .Instr(Instr), .DImmI(out_13));
  Multiplexer #(.Selector_Bits(3)) multiplexer_5 (
    .sel(ALU_B_MUX), .in_0(MEM_IN), .in_1(ImmI), .in_2(ImmS), .in_3(ImmB), .in_4(ImmU), .in_5(ImmJ),
    .in_6(Const1), .in_7(1'b0), .out(ALU_B));
  Clock clock_1 (
    .CLK(CLK), .nCLK(nCLK), .LEN(LEN), .LASTSTEP(LASTSTEP), .nRESET(nRESET), .STEP(out_12[4:0]),
    .LASTSUBSTEP(clock_1_lastsubstep), .nSTEPDONE(nSTEPDONE), .SUBSTEP(Substep), .nOPDONE(nOPDONE));
  and and_3 (BUS_CLK, CLK, BUS_EN);
  ALU alu_1 (
    .CLK(BUS_CLK), .A(ALU_A), .B(ALU_B), .N(ALU_N), .ALU_nRESET(nALU_RESET), .FLAG_LATCH(ALU_FLAG_LATCH),
    .S(ALU_OP), .SH_LOADLEN(alu_shift_step_1_sh_loadlen), .SH_nOUTPUT(alu_shift_step_1_nsh_output),
    .SH_RESET(alu_shift_step_1_sh_reset), .FLAG(out_12[14]), .OUT(ADDR_IN), .DLEN(out_36));  // open: DSUM, C
  or or_1 (BUS_EN, LEN[0], LEN[1]);
  Multiplexer #(.Selector_Bits(2)) multiplexer_6 (
    .sel(REG_IN_MUX), .in_0(ADDR_IN), .in_1(MEM_OUT), .in_2(MEPC_OUT), .in_3(PC_OUT), .out(REG_IN));
  Mem mem_1 (
    .CLK(CLK), .BUS_CLK(BUS_CLK), .IN(MEM_IN), .IN_ADDR(ADDR_IN), .LATCH_ADDR(ADDR_LATCH),
    .CLK_ADDR(ADDR_CLK), .nPE_ADDR(nADDR_PE), .nOE(nMEM_OE), .nWE(nMEM_WE), .nRESET(nRESET),
    .ROM_DATA(ROM_DATA), .nS_EXT(nS_EXT), .OUT(MEM_OUT), .ADDR(ADDR), .Dout(Dout), .DVal(Dval),
    .ROM_ADDR(ROM_ADDR), .ROM_SEL(ROM_SEL), .Din(ROM_DIN));  // open: DS
  Register_bank register_bank_1 (
    .CLK(BUS_CLK), .IN(REG_IN), .nEN_IN(nREG_IN_EN), .SA(RSA), .SB(RSB), .SD(RSD), .RESET(RESET), .A(RS1),
    .B(MEM_IN));
  ROM #(.AddrBits(16), .isProgramMemory("true"), .Bits(32)) MicroCode (
    .A(out_12), .sel(1'b1),
    .D({MicroCode_d[31], REG_IN_MUX, ALU_B_MUX, ALU_A_MUX, MicroCode_d[23:22], OP_LATCH, nMEM_WE, nMEM_OE, nADDR_PE, ADDR_CLK, ADDR_LATCH, MicroCode_d[15:12], PC_OUT_SnP, PC_IN_LATCH, nREG_IN_EN, LASTSTEP, LEN, ALU_OP, ALU_FLAG_LATCH, nALU_RESET, ALU_N}));
  EEPROM #(.AddrBits(16), .Bits(8)) Firmware (.A(ROM_ADDR), .CS(ROM_SEL), .WE(~nMEM_WE), .OE(~nMEM_OE), .D(ROM_DATA));
  assign ROM_DATA = ~nMEM_WE ? ROM_DIN : 8'bz;  // DriverInvSel driverinvsel_1

  assign Step = out_12[4:0];

  // Other names for the same wires on the sheet: PC_OUT_LATCH = LASTSTEP; PC_CNT_EN = OP_LATCH; ALU_OUT = ADDR_IN;
  //   CSR_ADDR_LATCH = in_21; CSR_IN = in_22; FLAG = out_12[14]; FUNC3[2:0] = out_12[12:10]; gp[31:0] = x3_gp;
  //   IMM_SnP = BUS_EN; Mem_Dout[7:0] = Dout; Mem_Dval[7:0] = Dval; OPCODE[4:0] = out_12[9:5]; PC_IN_MUX = in_11;
  //   RS2 = MEM_IN; SA = out_12[13]; SYS = out_12[15]

  // Notes on the sheet:
  //   CLK_RAW: Hz: 5000
  //   Debug
  //   Interrupts
  //   CSR
  //   Clock
  //   ALU
  //   PC
  //   Opcode
  //   Registers
  //   Memory
  //   Microcode
  //   ROM
  //   contents of MicroCode (hex, n*v repeats v):
  //   1d1c0a8a,190202,130202,1d0242,170202,1d0242,170202,1d0242,170202,1d0242,3d0202,1d0200,
  //   41c0282,190202,130202,201d0042,201d0042,201d0042,201d0042,201d0102,0,0,0,0,0,0,0,
  //   0,0,0,0,0,1d1c0a8a,190202,130202,1d0242,170202,1d0242,170202,1d0242,170202,1d0242,
  //   3d0202,3d0202,3d0202,3d0302,0,0,0,0,0,0,0,0,0,0,0,0,0,0,0,0,0,0,1d1c0a8a,190202,130202,
  //   1d0242,170202,1d0242,170202,1d0242,170202,1d0242,3d0202,3d0202,3d0202,3d0302,0,0,
  //   0,0,0,0,0,0,0,0,0,0,0,0,0,0,0,0,1d1c0a8a,190202,130202,1d0242,170202,1d0242,170202,
  //   1d0242,170202,1d0242,3d0202,3d0202,3d0202,3d0302,0,0,0,0,0,0,0,0,0,0,0,0,0,0,0,0,
  //   0,0,1d1c0a8a,190202,130202,1d0242,170202,1d0242,170202,1d0242,170202,1d0242,3d0202,
  //   1d0200,41d0082,1d0302,0,0,0,0,0,0,0,0,0,0,0,0,0,0,0,0,0,0,1d1c0a8a,190202,130202,
  //   1d0242,170202,1d0242,170202,1d0242,170202,1d0242,3d0202,1d0200,111d0882,1d0302,0,
  //   0,0,0,0,0,0,0,0,0,0,0,0,0,0,0,0,0,1d1c0a8a,190202,130202,1d0242,170202,1d0242,170202,
  //   1d0242,170202,1d0242,3d0202,3d0202,3d0202,3d0302,0,0,0,0,0,0,0,0,0,0,0,0,0,0,0,0,
  //   0,0,1d1c0a8a,190202,130202,1d0242,170202,1d0242,170202,1d0242,170202,1d0242,3d0202,
  //   3d0202,3d0202,3d0302,0,0,0,0,0,0,0,0,0,0,0,0,0,0,0,0,0,0,1d1c0a8a,190202,130202,1d0242,
  //   170202,1d0242,170202,1d0242,170202,1d0242,3d0202,1d0200,81c0282,190202,1a0242,c0202,
  //   1c0302,0,0,0,0,0,0,0,0,0,0,0,0,0,0,0,1d1c0a8a,190202,130202,1d0242,170202,1d0242,
  //   170202,1d0242,170202,1d0242,3d0202,3d0202,3d0202,3d0302,0,0,0,0,0,0,0,0,0,0,0,0,0,
  //   0,0,0,0,0,1d1c0a8a,190202,130202,1d0242,170202,1d0242,170202,1d0242,170202,1d0242,
  //   3d0202,3d0202,3d0202,3d0302,0,0,0,0,0,0,0,0,0,0,0,0,0,0,0,0,0,0,1d1c0a8a,190202,130202,
  //   1d0242,170202,1d0242,170202,1d0242,170202,1d0242,3d0202,3d0202,3d0202,3d0302,0,0,
  //   0,0,0,0,0,0,0,0,0,0,0,0,0,0,0,0,1d1c0a8a,190202,130202,1d0242,170202,1d0242,170202,
  //   1d0242,170202,1d0242,3d0202,1d0200,1d0082,1d0302,0,0,0,0,0,0,0,0,0,0,0,0,0,0,0,0,
  //   0,0,1d1c0a8a,190202,130202,1d0242,170202,1d0242,170202,1d0242,170202,1d0242,3d0202,
  //   1d0200,131d0082,1d0302,0,0,0,0,0,0,0,0,0,0,0,0,0,0,0,0,0,0,1d1c0a8a,190202,130202,
  //   1d0242,170202,1d0242,170202,1d0242,170202,1d0242,3d0202,3d0202,3d0202,3d0302,0,0,
  //   0,0,0,0,0,0,0,0,0,0,0,0,0,0,0,0,1d1c0a8a,190202,130202,1d0242,170202,1d0242,170202,
  //   1d0242,170202,1d0242,3d0202,3d0202,3d0202,3d0302,0,0,0,0,0,0,0,0,0,0,0,0,0,0,0,0,
  //   0,0,1d1c0a8a,190202,130202,1d0242,170202,1d0242,170202,1d0242,170202,1d0242,3d0202,
  //   3d0202,3d0202,3d0302,0,0,0,0,0,0,0,0,0,0,0,0,0,0,0,0,0,0,1d1c0a8a,190202,130202,1d0242,
  //   170202,1d0242,170202,1d0242,170202,1d0242,3d0202,3d0202,3d0202,3d0302,0,0,0,0,0,0,
  //   0,0,0,0,0,0,0,0,0,0,0,0,1d1c0a8a,190202,130202,1d0242,170202,1d0242,170202,1d0242,
  //   170202,1d0242,3d0202,3d0202,3d0202,3d0302,0,0,0,0,0,0,0,0,0,0,0,0,0,0,0,0,0,0,1d1c0a8a,
  //   190202,130202,1d0242,170202,1d0242,170202,1d0242,170202,1d0242,3d0202,3d0202,3d0202,
  //   3d0302,0,0,0,0,0,0,0,0,0,0,0,0,0,0,0,0,0,0,1d1c0a8a,190202,130202,1d0242,170202,1d0242,
  //   170202,1d0242,170202,1d0242,3d0202,3d0202,3d0202,3d0302,0,0,0,0,0,0,0,0,0,0,0,0,0,
  //   0,0,0,0,0,1d1c0a8a,190202,130202,1d0242,170202,1d0242,170202,1d0242,170202,1d0242,
  //   3d0202,3d0202,3d0202,3d0302,0,0,0,0,0,0,0,0,0,0,0,0,0,0,0,0,0,0,1d1c0a8a,190202,130202,
  //   1d0242,170202,1d0242,170202,1d0242,170202,1d0242,3d0202,3d0202,3d0202,3d0302,0,0,
  //   0,0,0,0,0,0,0,0,0,0,0,0,0,0,0,0,1d1c0a8a,190202,130202,1d0242,170202,1d0242,170202,
  //   1d0242,170202,1d0242,3d0202,3d0202,3d0202,3d0302,0,0,0,0,0,0,0,0,0,0,0,0,0,0,0,0,
  //   0,0,1d1c0a8a,190202,130202,1d0242,170202,1d0242,170202,1d0242,170202,1d0242,3d0202,
  //   1d0201,1d0293,1d0206,1d0302,0,0,0,0,0,0,0,0,0,0,0,0,0,0,0,0,0,1d1c0a8a,190202,130202,
  //   1d0242,170202,1d0242,170202,1d0242,170202,1d0242,3d0202,1d0200,41d0282,1d0600,1d1d08c2,
  //   1d1d0202,191d08c2,191d08c2,191d08c2,191d0842,191d0842,191d0842,1d0302,0,0,0,0,0,0,
  //   0,0,0,1d1c0a8a,190202,130202,1d0242,170202,1d0242,170202,1d0242,170202,1d0242,3d0202,
  //   3d0202,3d0202,3d0302,0,0,0,0,0,0,0,0,0,0,0,0,0,0,0,0,0,0,1d1c0a8a,190202,130202,1d0242,
  //   170202,1d0242,170202,1d0242,170202,1d0242,3d0202,1d0200,151d0a82,1d0600,1d1d08c2,
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  //   contents of Firmware (hex, n*v repeats v):
  //   13,4,10,1,93,0,10,0,13,1,0,0,33,97,20,0,93,3,10,0,93,4,20,0,63,10,77,54,93,0,10,0,
  //   13,1,10,0,33,97,20,0,93,3,20,0,93,4,30,0,63,14,77,52,93,0,10,0,13,1,70,0,33,97,20,
  //   0,93,3,0,8,93,4,40,0,63,18,77,50,93,0,10,0,13,1,e0,0,33,97,20,0,b7,43,0,0,93,4,50,
  //   0,63,1c,77,4e,93,0,10,0,13,1,f0,1,33,97,20,0,b7,3,0,80,93,4,60,0,63,10,77,4e,93,0,
  //   f0,ff,13,1,0,0,33,97,20,0,93,3,f0,ff,93,4,70,0,63,14,77,4c,93,0,f0,ff,13,1,10,0,33,
  //   97,20,0,93,3,e0,ff,93,4,80,0,63,18,77,4a,93,0,f0,ff,13,1,70,0,33,97,20,0,93,3,0,f8,
  //   93,4,90,0,63,1c,77,48,93,0,f0,ff,13,1,e0,0,33,97,20,0,b7,c3,ff,ff,93,4,a0,0,63,10,
  //   77,48,93,0,f0,ff,13,1,f0,1,33,97,20,0,b7,3,0,80,93,4,b0,0,63,14,77,46,b7,20,21,21,
  //   93,80,10,12,13,1,0,0,33,97,20,0,b7,23,21,21,93,83,13,12,93,4,c0,0,63,14,77,44,b7,
  //   20,21,21,93,80,10,12,13,1,10,0,33,97,20,0,b7,43,42,42,93,83,23,24,93,4,d0,0,63,14,
  //   77,42,b7,20,21,21,93,80,10,12,13,1,70,0,33,97,20,0,b7,93,90,90,93,83,3,8,93,4,e0,
  //   0,63,14,77,40,b7,20,21,21,93,80,10,12,13,1,e0,0,33,97,20,0,b7,43,48,48,93,4,f0,0,
  //   63,16,77,3e,b7,20,21,21,93,80,10,12,13,1,f0,1,33,97,20,0,b7,3,0,80,93,4,0,1,63,18,
  //   77,3c,b7,20,21,21,93,80,10,12,13,1,0,fc,33,97,20,0,b7,23,21,21,93,83,13,12,93,4,10,
  //   1,63,18,77,3a,b7,20,21,21,93,80,10,12,13,1,10,fc,33,97,20,0,b7,43,42,42,93,83,23,
  //   24,93,4,20,1,63,18,77,38,b7,20,21,21,93,80,10,12,13,1,70,fc,33,97,20,0,b7,93,90,90,
  //   93,83,3,8,93,4,30,1,63,18,77,36,b7,20,21,21,93,80,10,12,13,1,e0,fc,33,97,20,0,b7,
  //   43,48,48,93,4,40,1,63,1a,77,34,93,0,10,0,13,1,70,0,b3,90,20,0,93,3,0,8,93,4,60,1,
  //   63,9e,70,32,93,0,10,0,13,1,e0,0,33,91,20,0,b7,43,0,0,93,4,70,1,63,12,71,32,93,0,30,
  //   0,b3,90,10,0,93,3,80,1,93,4,80,1,63,98,70,30,13,2,0,0,93,0,10,0,13,1,70,0,33,97,20,
  //   0,13,3,7,0,13,2,12,0,93,2,20,0,e3,14,52,fe,93,3,0,8,93,4,90,1,63,12,73,2e,13,2,0,
  //   0,93,0,10,0,13,1,e0,0,33,97,20,0,13,0,0,0,13,3,7,0,13,2,12,0,93,2,20,0,e3,12,52,fe,
  //   b7,43,0,0,93,4,a0,1,63,1a,73,2a,13,2,0,0,93,0,10,0,13,1,f0,1,33,97,20,0,13,0,0,0,
  //   13,0,0,0,13,3,7,0,13,2,12,0,93,2,20,0,e3,10,52,fe,b7,3,0,80,93,4,b0,1,63,10,73,28,
  //   13,2,0,0,93,0,10,0,13,1,70,0,33,97,20,0,13,2,12,0,93,2,20,0,e3,16,52,fe,93,3,0,8,
  //   93,4,c0,1,63,1c,77,24,13,2,0,0,93,0,10,0,13,1,e0,0,13,0,0,0,33,97,20,0,13,2,12,0,
  //   93,2,20,0,e3,14,52,fe,b7,43,0,0,93,4,d0,1,63,16,77,22,13,2,0,0,93,0,10,0,13,1,f0,
  //   1,13,0,0,0,13,0,0,0,33,97,20,0,13,2,12,0,93,2,20,0,e3,12,52,fe,b7,3,0,80,93,4,e0,
  //   1,63,1e,77,1e,13,2,0,0,93,0,10,0,13,0,0,0,13,1,70,0,33,97,20,0,13,2,12,0,93,2,20,
  //   0,e3,14,52,fe,93,3,0,8,93,4,f0,1,63,18,77,1c,13,2,0,0,93,0,10,0,13,0,0,0,13,1,e0,
  //   0,13,0,0,0,33,97,20,0,13,2,12,0,93,2,20,0,e3,12,52,fe,b7,43,0,0,93,4,0,2,63,10,77,
  //   1a,13,2,0,0,93,0,10,0,13,0,0,0,13,0,0,0,13,1,f0,1,33,97,20,0,13,2,12,0,93,2,20,0,
  //   e3,12,52,fe,b7,3,0,80,93,4,10,2,63,18,77,16,13,2,0,0,13,1,70,0,93,0,10,0,33,97,20,
  //   0,13,2,12,0,93,2,20,0,e3,16,52,fe,93,3,0,8,93,4,20,2,63,14,77,14,13,2,0,0,13,1,e0,
  //   0,93,0,10,0,13,0,0,0,33,97,20,0,13,2,12,0,93,2,20,0,e3,14,52,fe,b7,43,0,0,93,4,30,
  //   2,63,1e,77,10,13,2,0,0,13,1,f0,1,93,0,10,0,13,0,0,0,13,0,0,0,33,97,20,0,13,2,12,0,
  //   93,2,20,0,e3,12,52,fe,b7,3,0,80,93,4,40,2,63,16,77,e,13,2,0,0,13,1,70,0,13,0,0,0,
  //   93,0,10,0,33,97,20,0,13,2,12,0,93,2,20,0,e3,14,52,fe,93,3,0,8,93,4,50,2,63,10,77,
  //   c,13,2,0,0,13,1,e0,0,13,0,0,0,93,0,10,0,13,0,0,0,33,97,20,0,13,2,12,0,93,2,20,0,e3,
  //   12,52,fe,b7,43,0,0,93,4,60,2,63,18,77,8,13,2,0,0,13,1,f0,1,13,0,0,0,13,0,0,0,93,0,
  //   10,0,33,97,20,0,13,2,12,0,93,2,20,0,e3,12,52,fe,b7,3,0,80,93,4,70,2,63,10,77,6,93,
  //   0,f0,0,33,11,10,0,93,3,0,0,93,4,80,2,63,16,71,4,93,0,0,2,33,91,0,0,93,3,0,2,93,4,
  //   90,2,63,1c,71,2,b3,10,0,0,93,3,0,0,93,4,a0,2,63,94,70,2,93,0,0,40,37,11,0,0,13,1,
  //   1,80,33,90,20,0,93,3,0,0,93,4,b0,2,63,16,70,0,63,4,90,0,6f,0,40,1,63,80,4,0,93,10,
  //   4,1,b3,81,90,0,6f,0,0,0,13,4,20,1,b7,0,0,80,13,1,0,0,33,d7,20,0,b7,3,0,80,93,4,20,
  //   0,63,1c,77,4c,b7,0,0,80,13,1,10,0,33,d7,20,0,b7,3,0,40,93,4,30,0,63,10,77,4c,b7,0,
  //   0,80,13,1,70,0,33,d7,20,0,b7,3,0,1,93,4,40,0,63,14,77,4a,b7,0,0,80,13,1,e0,0,33,d7,
  //   20,0,b7,3,2,0,93,4,50,0,63,18,77,48,b7,0,0,80,93,80,10,0,13,1,f0,1,33,d7,20,0,93,
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endmodule
